// Logisim project Booth.circ as structural Verilog: 11 circuits, main circuit main
module main (
);

  Display_4_bit_to_7_segment display_4_bit_to_7_segment_1 ();  // open: F, E, D, G, A, B, C, inp
endmodule

module Booth (
  input  [7:0] in_1,
  input  [7:0] in_2,
  input  reset,
  output [7:0] Multiplicand,
  output [7:0] Multiplier,
  output [15:0] Out
);

  wire display_4_bit_to_7_segment_1_a, display_4_bit_to_7_segment_1_b, display_4_bit_to_7_segment_1_c,
       display_4_bit_to_7_segment_1_d, display_4_bit_to_7_segment_1_e, display_4_bit_to_7_segment_1_f,
       display_4_bit_to_7_segment_1_g, display_4_bit_to_7_segment_2_a, display_4_bit_to_7_segment_2_b,
       display_4_bit_to_7_segment_2_c, display_4_bit_to_7_segment_2_d, display_4_bit_to_7_segment_2_e,
       display_4_bit_to_7_segment_2_f, display_4_bit_to_7_segment_2_g, display_4_bit_to_7_segment_3_a,
       display_4_bit_to_7_segment_3_b, display_4_bit_to_7_segment_3_c, display_4_bit_to_7_segment_3_d,
       display_4_bit_to_7_segment_3_e, display_4_bit_to_7_segment_3_f, display_4_bit_to_7_segment_3_g,
       display_4_bit_to_7_segment_4_a, display_4_bit_to_7_segment_4_b, display_4_bit_to_7_segment_4_c,
       display_4_bit_to_7_segment_4_d, display_4_bit_to_7_segment_4_e, display_4_bit_to_7_segment_4_f,
       display_4_bit_to_7_segment_4_g, display_4_bit_to_7_segment_5_a, display_4_bit_to_7_segment_5_b,
       display_4_bit_to_7_segment_5_c, display_4_bit_to_7_segment_5_d, display_4_bit_to_7_segment_5_e,
       display_4_bit_to_7_segment_5_f, display_4_bit_to_7_segment_5_g, display_4_bit_to_7_segment_6_a,
       display_4_bit_to_7_segment_6_b, display_4_bit_to_7_segment_6_c, display_4_bit_to_7_segment_6_d,
       display_4_bit_to_7_segment_6_e, display_4_bit_to_7_segment_6_f, display_4_bit_to_7_segment_6_g,
       display_4_bit_to_7_segment_7_a, display_4_bit_to_7_segment_7_b, display_4_bit_to_7_segment_7_c,
       display_4_bit_to_7_segment_7_d, display_4_bit_to_7_segment_7_e, display_4_bit_to_7_segment_7_f,
       display_4_bit_to_7_segment_7_g, display_4_bit_to_7_segment_8_a, display_4_bit_to_7_segment_8_b,
       display_4_bit_to_7_segment_8_c, display_4_bit_to_7_segment_8_d, display_4_bit_to_7_segment_8_e,
       display_4_bit_to_7_segment_8_f, display_4_bit_to_7_segment_8_g, InputGate_2_out_3, InputGate_out_3,
       right_shift_8_bit_1_out_5, right_shift_8_bit_1_out_6, sysclk_out;
  wire [15:0] big_and_1_out_3, Latch_q, left_shift_16_bit_1_out_5;

  Clock sysclk (.out(sysclk_out));
  _7_Segment_Display u_7_segment_display_1 (
    .g(display_4_bit_to_7_segment_1_g), .f(display_4_bit_to_7_segment_1_f),
    .a(display_4_bit_to_7_segment_1_a), .b(display_4_bit_to_7_segment_1_b),
    .e(display_4_bit_to_7_segment_1_e), .d(display_4_bit_to_7_segment_1_d), .c(display_4_bit_to_7_segment_1_c));  // open: dp
  Display_4_bit_to_7_segment display_4_bit_to_7_segment_1 (
    .F(display_4_bit_to_7_segment_1_f), .E(display_4_bit_to_7_segment_1_e),
    .D(display_4_bit_to_7_segment_1_d), .G(display_4_bit_to_7_segment_1_g),
    .A(display_4_bit_to_7_segment_1_a), .B(display_4_bit_to_7_segment_1_b),
    .C(display_4_bit_to_7_segment_1_c), .inp(in_1[7:4]));
  InputGate InputGate (.clk(sysclk_out), .reset(reset), .out_3(InputGate_out_3));
  _7_Segment_Display u_7_segment_display_2 (
    .g(display_4_bit_to_7_segment_2_g), .f(display_4_bit_to_7_segment_2_f),
    .a(display_4_bit_to_7_segment_2_a), .b(display_4_bit_to_7_segment_2_b),
    .e(display_4_bit_to_7_segment_2_e), .d(display_4_bit_to_7_segment_2_d), .c(display_4_bit_to_7_segment_2_c));  // open: dp
  Display_4_bit_to_7_segment display_4_bit_to_7_segment_2 (
    .F(display_4_bit_to_7_segment_2_f), .E(display_4_bit_to_7_segment_2_e),
    .D(display_4_bit_to_7_segment_2_d), .G(display_4_bit_to_7_segment_2_g),
    .A(display_4_bit_to_7_segment_2_a), .B(display_4_bit_to_7_segment_2_b),
    .C(display_4_bit_to_7_segment_2_c), .inp(in_1[3:0]));
  Left_Shift_16_bit left_shift_16_bit_1 (
    .reset(reset), .load(InputGate_out_3), .clk(sysclk_out), .in_1(in_1), .out_5(left_shift_16_bit_1_out_5));
  Big_And big_and_1 (.in_2(left_shift_16_bit_1_out_5), .out_3(big_and_1_out_3), .in_1(right_shift_8_bit_1_out_6));
  Full_Adder_16_bit full_adder_16_bit_1 (
    .Output(Out), .ControlBit(right_shift_8_bit_1_out_5), .Input_Y(big_and_1_out_3), .Input_X(Latch_q));  // open: Cout
  _7_Segment_Display u_7_segment_display_3 (
    .g(display_4_bit_to_7_segment_3_g), .f(display_4_bit_to_7_segment_3_f),
    .a(display_4_bit_to_7_segment_3_a), .b(display_4_bit_to_7_segment_3_b),
    .e(display_4_bit_to_7_segment_3_e), .d(display_4_bit_to_7_segment_3_d), .c(display_4_bit_to_7_segment_3_c));  // open: dp
  Display_4_bit_to_7_segment display_4_bit_to_7_segment_3 (
    .F(display_4_bit_to_7_segment_3_f), .E(display_4_bit_to_7_segment_3_e),
    .D(display_4_bit_to_7_segment_3_d), .G(display_4_bit_to_7_segment_3_g),
    .A(display_4_bit_to_7_segment_3_a), .B(display_4_bit_to_7_segment_3_b),
    .C(display_4_bit_to_7_segment_3_c), .inp(in_2[7:4]));
  InputGate InputGate_2 (.clk(sysclk_out), .reset(reset), .out_3(InputGate_2_out_3));
  Register #(.width(16)) Latch (.D(Out), .en(1'b1), .clk(sysclk_out), .Q(Latch_q), .clr(reset));
  _7_Segment_Display u_7_segment_display_4 (
    .g(display_4_bit_to_7_segment_4_g), .f(display_4_bit_to_7_segment_4_f),
    .a(display_4_bit_to_7_segment_4_a), .b(display_4_bit_to_7_segment_4_b),
    .e(display_4_bit_to_7_segment_4_e), .d(display_4_bit_to_7_segment_4_d), .c(display_4_bit_to_7_segment_4_c));  // open: dp
  Display_4_bit_to_7_segment display_4_bit_to_7_segment_4 (
    .F(display_4_bit_to_7_segment_4_f), .E(display_4_bit_to_7_segment_4_e),
    .D(display_4_bit_to_7_segment_4_d), .G(display_4_bit_to_7_segment_4_g),
    .A(display_4_bit_to_7_segment_4_a), .B(display_4_bit_to_7_segment_4_b),
    .C(display_4_bit_to_7_segment_4_c), .inp(in_2[3:0]));
  _7_Segment_Display u_7_segment_display_5 (
    .g(display_4_bit_to_7_segment_5_g), .f(display_4_bit_to_7_segment_5_f),
    .a(display_4_bit_to_7_segment_5_a), .b(display_4_bit_to_7_segment_5_b),
    .e(display_4_bit_to_7_segment_5_e), .d(display_4_bit_to_7_segment_5_d), .c(display_4_bit_to_7_segment_5_c));  // open: dp
  Display_4_bit_to_7_segment display_4_bit_to_7_segment_5 (
    .F(display_4_bit_to_7_segment_5_f), .E(display_4_bit_to_7_segment_5_e),
    .D(display_4_bit_to_7_segment_5_d), .G(display_4_bit_to_7_segment_5_g),
    .A(display_4_bit_to_7_segment_5_a), .B(display_4_bit_to_7_segment_5_b),
    .C(display_4_bit_to_7_segment_5_c), .inp(Out[15:12]));
  Right_Shift_8_bit right_shift_8_bit_1 (
    .Load(InputGate_2_out_3), .clk(sysclk_out), .inp(in_2), .out_6(right_shift_8_bit_1_out_6),
    .out_5(right_shift_8_bit_1_out_5), .reset(reset));
  Display_4_bit_to_7_segment display_4_bit_to_7_segment_6 (
    .F(display_4_bit_to_7_segment_6_f), .E(display_4_bit_to_7_segment_6_e),
    .D(display_4_bit_to_7_segment_6_d), .G(display_4_bit_to_7_segment_6_g),
    .A(display_4_bit_to_7_segment_6_a), .B(display_4_bit_to_7_segment_6_b),
    .C(display_4_bit_to_7_segment_6_c), .inp(Out[11:8]));
  _7_Segment_Display u_7_segment_display_6 (
    .g(display_4_bit_to_7_segment_6_g), .f(display_4_bit_to_7_segment_6_f),
    .a(display_4_bit_to_7_segment_6_a), .b(display_4_bit_to_7_segment_6_b),
    .e(display_4_bit_to_7_segment_6_e), .d(display_4_bit_to_7_segment_6_d), .c(display_4_bit_to_7_segment_6_c));  // open: dp
  Display_4_bit_to_7_segment display_4_bit_to_7_segment_7 (
    .F(display_4_bit_to_7_segment_7_f), .E(display_4_bit_to_7_segment_7_e),
    .D(display_4_bit_to_7_segment_7_d), .G(display_4_bit_to_7_segment_7_g),
    .A(display_4_bit_to_7_segment_7_a), .B(display_4_bit_to_7_segment_7_b),
    .C(display_4_bit_to_7_segment_7_c), .inp(Out[7:4]));
  _7_Segment_Display u_7_segment_display_7 (
    .g(display_4_bit_to_7_segment_7_g), .f(display_4_bit_to_7_segment_7_f),
    .a(display_4_bit_to_7_segment_7_a), .b(display_4_bit_to_7_segment_7_b),
    .e(display_4_bit_to_7_segment_7_e), .d(display_4_bit_to_7_segment_7_d), .c(display_4_bit_to_7_segment_7_c));  // open: dp
  _7_Segment_Display u_7_segment_display_8 (
    .g(display_4_bit_to_7_segment_8_g), .f(display_4_bit_to_7_segment_8_f),
    .a(display_4_bit_to_7_segment_8_a), .b(display_4_bit_to_7_segment_8_b),
    .e(display_4_bit_to_7_segment_8_e), .d(display_4_bit_to_7_segment_8_d), .c(display_4_bit_to_7_segment_8_c));  // open: dp
  Display_4_bit_to_7_segment display_4_bit_to_7_segment_8 (
    .F(display_4_bit_to_7_segment_8_f), .E(display_4_bit_to_7_segment_8_e),
    .D(display_4_bit_to_7_segment_8_d), .G(display_4_bit_to_7_segment_8_g),
    .A(display_4_bit_to_7_segment_8_a), .B(display_4_bit_to_7_segment_8_b),
    .C(display_4_bit_to_7_segment_8_c), .inp(Out[3:0]));

  assign Multiplicand = in_1;
  assign Multiplier = in_2;
endmodule

// Display_4_bit_7_seg
module Display_4_bit_to_7_segment (
  input  [3:0] inp,
  output F,
  output E,
  output D,
  output G,
  output A,
  output B,
  output C
);

  wire and_1_out, and_2_out, and_3_out, and_4_out, and_5_out, and_6_out, and_7_out, and_8_out, and_9_out,
       and_10_out, and_11_out, and_12_out, and_13_out, and_14_out, and_15_out, and_16_out, not_1_out,
       not_2_out, not_3_out, not_4_out;

  not not_1 (not_1_out, inp[3]);
  not not_2 (not_2_out, inp[1]);
  not not_3 (not_3_out, inp[2]);
  not not_4 (not_4_out, inp[0]);
  and and_1 (and_1_out, inp[0], inp[1], inp[2], inp[3]);
  and and_2 (and_2_out, not_4_out, inp[1], inp[2], inp[3]);
  and and_3 (and_3_out, inp[0], not_2_out, inp[2], inp[3]);
  and and_4 (and_4_out, not_4_out, not_2_out, inp[2], inp[3]);
  and and_5 (and_5_out, inp[0], inp[1], not_3_out, inp[3]);
  and and_6 (and_6_out, not_4_out, inp[1], not_3_out, inp[3]);
  and and_7 (and_7_out, inp[0], not_2_out, not_3_out, inp[3]);
  and and_8 (and_8_out, not_4_out, not_2_out, not_3_out, inp[3]);
  and and_9 (and_9_out, inp[0], inp[1], inp[2], not_1_out);
  and and_10 (and_10_out, not_4_out, inp[1], inp[2], not_1_out);
  and and_11 (and_11_out, inp[0], not_2_out, inp[2], not_1_out);
  and and_12 (and_12_out, not_4_out, not_2_out, inp[2], not_1_out);
  and and_13 (and_13_out, inp[0], inp[1], not_3_out, not_1_out);
  and and_14 (and_14_out, not_4_out, inp[1], not_3_out, not_1_out);
  and and_15 (and_15_out, inp[0], not_2_out, not_3_out, not_1_out);
  and and_16 (and_16_out, not_4_out, not_2_out, not_3_out, not_1_out);
  nor nor_1 (F, and_15_out, and_14_out, and_13_out, and_9_out, and_3_out);
  nor nor_2 (E, and_15_out, and_13_out, and_12_out, and_11_out, and_9_out, and_7_out);
  nor nor_3 (D, and_15_out, and_12_out, and_9_out, and_6_out, and_1_out);
  nor nor_4 (G, and_16_out, and_15_out, and_9_out, and_4_out);
  nor nor_5 (A, and_15_out, and_12_out, and_5_out, and_3_out);
  nor nor_6 (C, and_14_out, and_4_out, and_2_out, and_1_out);
  nor nor_7 (B, and_11_out, and_10_out, and_5_out, and_4_out, and_2_out, and_1_out);

  // Notes on the sheet:
  //   7-segment display
  //   F
  //   E
  //   D
  //   C
  //   B
  //   A
  //   9
  //   8
  //   7
  //   6
  //   5
  //   4
  //   3
  //   2
  //   1
  //   0
endmodule

// FA_16_bit
module Full_Adder_16_bit (
  input  ControlBit,
  input  [15:0] Input_X,
  input  [15:0] Input_Y,
  output [15:0] Output,
  output Cout
);

  wire full_adder_1_bit_1_cout, full_adder_1_bit_2_cout, full_adder_1_bit_3_cout, full_adder_1_bit_4_cout,
       full_adder_1_bit_5_cout, full_adder_1_bit_6_cout, full_adder_1_bit_7_cout, full_adder_1_bit_8_cout,
       full_adder_1_bit_9_cout, full_adder_1_bit_10_cout, full_adder_1_bit_11_cout, full_adder_1_bit_12_cout,
       full_adder_1_bit_13_cout, full_adder_1_bit_14_cout, full_adder_1_bit_15_cout, xor_1_out, xor_2_out,
       xor_3_out, xor_4_out, xor_5_out, xor_6_out, xor_7_out, xor_8_out, xor_9_out, xor_10_out, xor_11_out,
       xor_12_out, xor_13_out, xor_14_out, xor_15_out, xor_16_out;

  xor xor_1 (xor_1_out, Input_Y[0], ControlBit);
  xor xor_2 (xor_2_out, Input_Y[1], ControlBit);
  xor xor_3 (xor_3_out, Input_Y[2], ControlBit);
  xor xor_4 (xor_4_out, Input_Y[3], ControlBit);
  xor xor_5 (xor_5_out, Input_Y[4], ControlBit);
  xor xor_6 (xor_6_out, Input_Y[5], ControlBit);
  xor xor_7 (xor_7_out, Input_Y[6], ControlBit);
  xor xor_8 (xor_8_out, Input_Y[7], ControlBit);
  xor xor_9 (xor_9_out, Input_Y[8], ControlBit);
  xor xor_10 (xor_10_out, Input_Y[9], ControlBit);
  xor xor_11 (xor_11_out, Input_Y[10], ControlBit);
  xor xor_12 (xor_12_out, Input_Y[11], ControlBit);
  xor xor_13 (xor_13_out, Input_Y[12], ControlBit);
  xor xor_14 (xor_14_out, Input_Y[13], ControlBit);
  xor xor_15 (xor_15_out, Input_Y[14], ControlBit);
  xor xor_16 (xor_16_out, Input_Y[15], ControlBit);
  Full_Adder_1_bit full_adder_1_bit_1 (
    .Cin(ControlBit), .Input_A(xor_1_out), .Input_B(Input_X[0]), .S(Output[0]), .Cout(full_adder_1_bit_1_cout));
  Full_Adder_1_bit full_adder_1_bit_2 (
    .Cin(full_adder_1_bit_1_cout), .Input_A(xor_2_out), .Input_B(Input_X[1]), .S(Output[1]),
    .Cout(full_adder_1_bit_2_cout));
  Full_Adder_1_bit full_adder_1_bit_3 (
    .Cin(full_adder_1_bit_2_cout), .Input_A(xor_3_out), .Input_B(Input_X[2]), .S(Output[2]),
    .Cout(full_adder_1_bit_3_cout));
  Full_Adder_1_bit full_adder_1_bit_4 (
    .Cin(full_adder_1_bit_3_cout), .Input_A(xor_4_out), .Input_B(Input_X[3]), .S(Output[3]),
    .Cout(full_adder_1_bit_4_cout));
  Full_Adder_1_bit full_adder_1_bit_5 (
    .Cin(full_adder_1_bit_4_cout), .Input_A(xor_5_out), .Input_B(Input_X[4]), .S(Output[4]),
    .Cout(full_adder_1_bit_5_cout));
  Full_Adder_1_bit full_adder_1_bit_6 (
    .Cin(full_adder_1_bit_5_cout), .Input_A(xor_6_out), .Input_B(Input_X[5]), .S(Output[5]),
    .Cout(full_adder_1_bit_6_cout));
  Full_Adder_1_bit full_adder_1_bit_7 (
    .Cin(full_adder_1_bit_6_cout), .Input_A(xor_7_out), .Input_B(Input_X[6]), .S(Output[6]),
    .Cout(full_adder_1_bit_7_cout));
  Full_Adder_1_bit full_adder_1_bit_8 (
    .Cin(full_adder_1_bit_7_cout), .Input_A(xor_8_out), .Input_B(Input_X[7]), .S(Output[7]),
    .Cout(full_adder_1_bit_8_cout));
  Full_Adder_1_bit full_adder_1_bit_9 (
    .Cin(full_adder_1_bit_8_cout), .Input_A(xor_9_out), .Input_B(Input_X[8]), .S(Output[8]),
    .Cout(full_adder_1_bit_9_cout));
  Full_Adder_1_bit full_adder_1_bit_10 (
    .Cin(full_adder_1_bit_9_cout), .Input_A(xor_10_out), .Input_B(Input_X[9]), .S(Output[9]),
    .Cout(full_adder_1_bit_10_cout));
  Full_Adder_1_bit full_adder_1_bit_11 (
    .Cin(full_adder_1_bit_10_cout), .Input_A(xor_11_out), .Input_B(Input_X[10]), .S(Output[10]),
    .Cout(full_adder_1_bit_11_cout));
  Full_Adder_1_bit full_adder_1_bit_12 (
    .Cin(full_adder_1_bit_11_cout), .Input_A(xor_12_out), .Input_B(Input_X[11]), .S(Output[11]),
    .Cout(full_adder_1_bit_12_cout));
  Full_Adder_1_bit full_adder_1_bit_13 (
    .Cin(full_adder_1_bit_12_cout), .Input_A(xor_13_out), .Input_B(Input_X[12]), .S(Output[12]),
    .Cout(full_adder_1_bit_13_cout));
  Full_Adder_1_bit full_adder_1_bit_14 (
    .Cin(full_adder_1_bit_13_cout), .Input_A(xor_14_out), .Input_B(Input_X[13]), .S(Output[13]),
    .Cout(full_adder_1_bit_14_cout));
  Full_Adder_1_bit full_adder_1_bit_15 (
    .Cin(full_adder_1_bit_14_cout), .Input_A(xor_15_out), .Input_B(Input_X[14]), .S(Output[14]),
    .Cout(full_adder_1_bit_15_cout));
  Full_Adder_1_bit full_adder_1_bit_16 (
    .Cin(full_adder_1_bit_15_cout), .Input_A(xor_16_out), .Input_B(Input_X[15]), .S(Output[15]), .Cout(Cout));
endmodule

module Full_Adder_1_bit (
  input  Cin,
  input  Input_A,
  input  Input_B,
  output S,
  output Cout
);

  wire half_adder_1bit_1_cout, half_adder_1bit_1_sum, half_adder_1bit_2_cout;

  Half_Adder_1bit half_adder_1bit_1 (
    .A(Input_A), .B(Input_B), .Sum(half_adder_1bit_1_sum), .Cout(half_adder_1bit_1_cout));
  Half_Adder_1bit half_adder_1bit_2 (.A(Cin), .B(half_adder_1bit_1_sum), .Sum(S), .Cout(half_adder_1bit_2_cout));
  or or_1 (Cout, half_adder_1bit_2_cout, half_adder_1bit_1_cout);

  // Notes on the sheet:
  //   Cin
  //   A
  //   B
  //   S
  //   Cout
endmodule

module Half_Adder_1bit (
  input  A,
  input  B,
  output Sum,
  output Cout
);

  xor xor_1 (Sum, A, B);
  and and_1 (Cout, A, B);
endmodule

module InputGate (
  input  clk,
  input  reset,
  output out_3
);

  wire d_ff_1_q, or_1_out;

  D_Flip_Flop d_ff_1 (.D(or_1_out), .clk(clk), .Q(d_ff_1_q), .Qn(out_3), .reset(reset));  // open: preset
  or or_1 (or_1_out, d_ff_1_q, out_3);
endmodule

module Left_Shift_16_bit (
  input  [7:0] in_1,
  input  load,
  input  clk,
  input  reset,
  output [15:0] out_5
);

  wire left_shift_8_bit_2_out_6;
  wire [7:0] bit_extender_1_out;

  assign bit_extender_1_out = {{7{in_1[7]}}, in_1[7]};  // Bit_Extender bit_extender_1
  Left_Shift_8_bit left_shift_8_bit_1 (
    .inp(bit_extender_1_out), .load(load), .clk(clk), .shift_in(left_shift_8_bit_2_out_6), .out(out_5[15:8]),
    .reset(reset));  // open: out_6
  Left_Shift_8_bit left_shift_8_bit_2 (
    .inp(in_1), .load(load), .clk(clk), .shift_in(1'b0), .out(out_5[7:0]), .reset(reset),
    .out_6(left_shift_8_bit_2_out_6));
endmodule

module Right_Shift_8_bit (
  input  clk,
  input  reset,
  input  Load,
  input  [7:0] inp,
  output out_5,
  output out_6
);

  wire and_1_out, and_2_out, and_3_out, and_4_out, and_5_out, and_6_out, and_7_out, and_8_out, and_9_out,
       and_10_out, and_11_out, and_12_out, and_13_out, and_14_out, and_16_out, and_17_out, d_ff_1_q,
       d_ff_2_q, d_ff_3_q, d_ff_4_q, d_ff_5_q, d_ff_6_q, d_ff_7_q, d_ff_8_q, d_ff_9_q, not_1_out, or_1_out,
       or_2_out, or_3_out, or_4_out, or_5_out, or_6_out, or_7_out, or_8_out;

  and and_1 (and_1_out, d_ff_1_q, not_1_out);
  not not_1 (not_1_out, Load);
  D_Flip_Flop d_ff_1 (.D(or_1_out), .clk(clk), .Q(d_ff_1_q), .reset(reset));  // open: Qn, preset
  or or_1 (or_1_out, and_1_out, and_2_out);
  and and_2 (and_2_out, Load, inp[7]);
  or or_2 (or_2_out, and_3_out, and_4_out);
  and and_3 (and_3_out, d_ff_1_q, not_1_out);
  D_Flip_Flop d_ff_2 (.D(or_2_out), .clk(clk), .Q(d_ff_2_q), .reset(reset));  // open: Qn, preset
  and and_4 (and_4_out, Load, inp[6]);
  D_Flip_Flop d_ff_3 (.D(or_3_out), .clk(clk), .Q(d_ff_3_q), .reset(reset));  // open: Qn, preset
  or or_3 (or_3_out, and_5_out, and_6_out);
  and and_5 (and_5_out, d_ff_2_q, not_1_out);
  and and_6 (and_6_out, Load, inp[5]);
  or or_4 (or_4_out, and_7_out, and_8_out);
  and and_7 (and_7_out, d_ff_3_q, not_1_out);
  D_Flip_Flop d_ff_4 (.D(or_4_out), .clk(clk), .Q(d_ff_4_q), .reset(reset));  // open: Qn, preset
  and and_8 (and_8_out, Load, inp[4]);
  D_Flip_Flop d_ff_5 (.D(or_5_out), .clk(clk), .Q(d_ff_5_q), .reset(reset));  // open: Qn, preset
  or or_5 (or_5_out, and_10_out, and_9_out);
  and and_9 (and_9_out, Load, inp[3]);
  and and_10 (and_10_out, d_ff_4_q, not_1_out);
  or or_6 (or_6_out, and_11_out, and_12_out);
  and and_11 (and_11_out, d_ff_5_q, not_1_out);
  D_Flip_Flop d_ff_6 (.D(or_6_out), .clk(clk), .Q(d_ff_6_q), .reset(reset));  // open: Qn, preset
  and and_12 (and_12_out, Load, inp[2]);
  D_Flip_Flop d_ff_7 (.D(or_7_out), .clk(clk), .Q(d_ff_7_q), .reset(reset));  // open: Qn, preset
  or or_7 (or_7_out, and_13_out, and_14_out);
  and and_13 (and_13_out, d_ff_6_q, not_1_out);
  and and_14 (and_14_out, Load, inp[1]);
  and and_15 (out_5, ~d_ff_9_q, d_ff_8_q);  // AND_Gate
  xor xor_1 (out_6, d_ff_9_q, d_ff_8_q);
  or or_8 (or_8_out, and_16_out, and_17_out);
  and and_16 (and_16_out, d_ff_7_q, not_1_out);
  D_Flip_Flop d_ff_8 (.D(or_8_out), .clk(clk), .Q(d_ff_8_q), .reset(reset));  // open: Qn, preset
  and and_17 (and_17_out, Load, inp[0]);
  D_Flip_Flop d_ff_9 (.D(d_ff_8_q), .clk(clk), .Q(d_ff_9_q), .reset(reset));  // open: Qn, preset
endmodule

module Left_Shift_8_bit (
  input  [7:0] inp,
  input  load,
  input  clk,
  input  shift_in,
  input  reset,
  output out_6,
  output [7:0] out
);

  wire and_1_out, and_2_out, and_3_out, and_4_out, and_5_out, and_6_out, and_7_out, and_8_out, and_9_out,
       and_10_out, and_11_out, and_12_out, and_13_out, and_14_out, and_15_out, and_16_out, not_1_out,
       or_1_out, or_2_out, or_3_out, or_4_out, or_5_out, or_6_out, or_7_out, or_8_out;

  not not_1 (not_1_out, load);
  and and_1 (and_1_out, inp[7], load);
  D_Flip_Flop d_ff_1 (.D(or_1_out), .clk(clk), .Q(out[7]), .reset(reset));  // open: Qn, preset
  or or_1 (or_1_out, and_1_out, and_2_out);
  and and_2 (and_2_out, not_1_out, out[6]);
  and and_3 (and_3_out, inp[6], load);
  D_Flip_Flop d_ff_2 (.D(or_2_out), .clk(clk), .Q(out[6]), .reset(reset));  // open: Qn, preset
  or or_2 (or_2_out, and_3_out, and_4_out);
  and and_4 (and_4_out, not_1_out, out[5]);
  and and_5 (and_5_out, inp[5], load);
  D_Flip_Flop d_ff_3 (.D(or_3_out), .clk(clk), .Q(out[5]), .reset(reset));  // open: Qn, preset
  or or_3 (or_3_out, and_5_out, and_6_out);
  and and_6 (and_6_out, not_1_out, out[4]);
  and and_7 (and_7_out, inp[4], load);
  D_Flip_Flop d_ff_4 (.D(or_4_out), .clk(clk), .Q(out[4]), .reset(reset));  // open: Qn, preset
  or or_4 (or_4_out, and_7_out, and_8_out);
  and and_8 (and_8_out, not_1_out, out[3]);
  and and_9 (and_9_out, inp[3], load);
  D_Flip_Flop d_ff_5 (.D(or_5_out), .clk(clk), .Q(out[3]), .reset(reset));  // open: Qn, preset
  or or_5 (or_5_out, and_9_out, and_10_out);
  and and_10 (and_10_out, not_1_out, out[2]);
  and and_11 (and_11_out, inp[2], load);
  D_Flip_Flop d_ff_6 (.D(or_6_out), .clk(clk), .Q(out[2]), .reset(reset));  // open: Qn, preset
  or or_6 (or_6_out, and_11_out, and_12_out);
  and and_12 (and_12_out, not_1_out, out[1]);
  and and_13 (and_13_out, inp[1], load);
  D_Flip_Flop d_ff_7 (.D(or_7_out), .clk(clk), .Q(out[1]), .reset(reset));  // open: Qn, preset
  or or_7 (or_7_out, and_13_out, and_14_out);
  and and_14 (and_14_out, not_1_out, out[0]);
  and and_15 (and_15_out, inp[0], load);
  D_Flip_Flop d_ff_8 (.D(or_8_out), .clk(clk), .Q(out[0]), .reset(reset));  // open: Qn, preset
  or or_8 (or_8_out, and_15_out, and_16_out);
  and and_16 (and_16_out, not_1_out, shift_in);

  assign out_6 = out[7];
endmodule

module Big_And (
  input  in_1,
  input  [15:0] in_2,
  output [15:0] out_3
);

  Multiplexer #(.width(16), .enable("false")) multiplexer_1 (.in0({16{1'b0}}), .in1(in_2), .out(out_3), .sel(in_1));
endmodule
