// Logisim project Shifter.circ as structural Verilog: 3 circuits, main circuit main
module main (
  input  [7:0] in_1,
  input  in_2,
  output out_3,
  output out_4,
  output [7:0] out_5
);

  wire clock_1_out, d_ff_1_q, rightshift8bit_1_out_7;

  Clock clock_1 (.out(clock_1_out));
  D_Flip_Flop d_ff_1 (.D(rightshift8bit_1_out_7), .clk(clock_1_out), .Q(d_ff_1_q));  // open: Qn, preset, reset
  RightShift8bit rightshift8bit_1 (
    .in_1(d_ff_1_q), .in_2(in_1), .in_3(in_2), .in_4(clock_1_out), .out_5(out_3), .out_6(out_4),
    .out_7(rightshift8bit_1_out_7), .out_8(out_5));
endmodule

module LefttShift16bit (
  input  [15:0] in_1,
  input  in_2,
  input  in_3,
  output [15:0] out_4
);

  wire [3:0] bit_extender_1_out;
  wire [15:0] register_1_q;

  assign bit_extender_1_out = {{3{in_2}}, in_2};  // Bit_Extender bit_extender_1
  Register #(.width(16)) register_1 (.D(in_1), .en(1'b1), .clk(in_3), .Q(register_1_q));  // open: clr
  Shifter #(.width(16)) shifter_1 (.in(register_1_q), .\dist (bit_extender_1_out), .out(out_4));
endmodule

module RightShift8bit (
  input  in_1,
  input  [7:0] in_2,
  input  in_3,
  input  in_4,
  output out_5,
  output out_6,
  output out_7,
  output [7:0] out_8
);

  wire bitselector_1_out;
  wire [2:0] bit_extender_1_out;
  wire [7:0] register_1_q;

  assign bit_extender_1_out = {{2{1'b0}}, in_3};  // Bit_Extender bit_extender_1
  BitSelector bitselector_1 (.in(in_2), .out(bitselector_1_out), .sel(3'b000));
  Register register_1 (.D(in_2), .en(1'b1), .clk(in_4), .Q(register_1_q));  // open: clr
  BitSelector bitselector_2 (.in(register_1_q), .out(out_7), .sel(3'b000));
  Shifter #(.shift("ar")) shifter_1 (.in(register_1_q), .\dist (bit_extender_1_out), .out(out_8));
  xor xor_1 (out_5, in_1, bitselector_1_out);
  and and_1 (out_6, bitselector_1_out, ~in_1);  // AND_Gate
endmodule
